// Logisim project respostas.circ as structural Verilog: 5 circuits, main circuit 01a
module _01a (
  input  x,
  input  y,
  input  z,
  output s1
);

  wire nor_1_out, not_1_out, not_2_out;

  not not_1 (not_1_out, y);
  not not_2 (not_2_out, z);
  nor nor_1 (nor_1_out, not_1_out, not_2_out);
  and and_1 (s1, x, nor_1_out);
endmodule

module _01b (
  input  x,
  input  y,
  input  z,
  output s1
);

  wire nor_1_out, not_1_out;

  not not_1 (not_1_out, x);
  nor nor_1 (nor_1_out, not_1_out, y);
  and and_1 (s1, nor_1_out, z);
endmodule

module _01c (
  input  x,
  input  y,
  input  z,
  output s1
);

  wire nand_1_out, not_1_out, not_2_out;

  not not_1 (not_1_out, x);
  not not_2 (not_2_out, y);
  nand nand_1 (nand_1_out, not_1_out, not_2_out);
  and and_1 (s1, nand_1_out, z);
endmodule

module _01d (
  input  x,
  input  y,
  input  z,
  output s1
);

  wire nand_1_out, not_1_out;

  not not_1 (not_1_out, y);
  nand nand_1 (nand_1_out, x, not_1_out);
  and and_1 (s1, nand_1_out, z);
endmodule

module _01e (
  input  x,
  input  y,
  input  z,
  output s1
);

  wire not_1_out, not_2_out, not_3_out, or_1_out, or_2_out;

  not not_1 (not_1_out, x);
  not not_2 (not_2_out, y);
  not not_3 (not_3_out, z);
  or or_1 (or_1_out, not_1_out, y);
  or or_2 (or_2_out, not_2_out, not_3_out);
  and and_1 (s1, or_1_out, or_2_out);
endmodule
