// Logisim project Logisim.circ as structural Verilog: 6 circuits, main circuit 01
module _01 (
  input  a,
  input  b,
  output y
);

  wire not_1_out, not_2_out;

  not not_1 (not_1_out, a);
  not not_2 (not_2_out, b);
  and and_1 (y, not_1_out, not_2_out);
endmodule

module _02 (
  input  a,
  input  b,
  output y
);

  wire not_1_out;

  not not_1 (not_1_out, b);
  or or_1 (y, a, not_1_out);
endmodule

module _03 (
  input  a,
  input  b,
  output y
);

  wire not_1_out, not_2_out;

  not not_1 (not_1_out, a);
  not not_2 (not_2_out, b);
  or or_1 (y, not_1_out, not_2_out);
endmodule

module _04 (
  input  a,
  input  b,
  output y
);

  wire not_1_out;

  not not_1 (not_1_out, a);
  nand nand_1 (y, not_1_out, b);
endmodule

module _05 (
  input  a,
  input  b,
  output y
);

  xnor xnor_1 (y, a, b);
endmodule

module _06 (
  input  a,
  input  b,
  output y
);

  xor xor_1 (y, a, b);
endmodule
