// Logisim project Logisim.circ as structural Verilog
module Q1 (
  input  x,
  input  x_2,
  input  y,
  input  z,
  input  y_2,
  input  z_2,
  input  x_3,
  input  y_3,
  input  x_4,
  input  z_3,
  input  y_4,
  input  z_4,
  input  x_5,
  input  y_5,
  input  z_5,
  output out_16,
  output out_17,
  output out_18,
  output out_19,
  output out_20
);

  wire and_1_out, and_2_out, and_3_out, and_4_out, and_5_out, and_6_out, and_7_out, and_8_out, and_9_out,
       and_10_out, and_11_out, and_12_out, and_13_out, not_1_out, not_2_out, not_3_out, not_4_out, not_5_out,
       not_6_out, not_7_out, not_8_out, not_9_out, not_10_out, not_11_out, not_12_out, not_13_out;

  not not_1 (not_1_out, x_5);
  not not_2 (not_2_out, y_5);
  not not_3 (not_3_out, z_5);
  not not_4 (not_4_out, z);
  not not_5 (not_5_out, x_3);
  not not_6 (not_6_out, y_3);
  not not_7 (not_7_out, z_3);
  and and_1 (and_1_out, x, y);
  and and_2 (and_2_out, y, not_4_out);
  and and_3 (and_3_out, x_3, not_6_out);
  and and_4 (and_4_out, not_6_out, not_7_out);
  or or_1 (out_16, and_1_out, and_2_out);
  or or_2 (out_18, and_3_out, and_4_out);
  and and_5 (and_5_out, x_5, not_2_out);
  and and_6 (and_6_out, not_1_out, z_5);
  and and_7 (and_7_out, not_2_out, z_5);
  or or_3 (out_20, and_6_out, and_7_out);
  not not_8 (not_8_out, x_2);
  not not_9 (not_9_out, y_2);
  not not_10 (not_10_out, z_2);
  not not_11 (not_11_out, x_4);
  not not_12 (not_12_out, y_4);
  not not_13 (not_13_out, z_4);
  and and_8 (and_8_out, not_8_out, not_9_out);
  and and_9 (and_9_out, x_2, not_10_out);
  and and_10 (and_10_out, y_2, not_10_out);
  and and_11 (and_11_out, x_4, not_12_out);
  and and_12 (and_12_out, y_4, not_13_out);
  and and_13 (and_13_out, not_13_out, x_4);
  or or_4 (out_17, and_8_out, and_9_out, and_10_out);
  or or_5 (out_19, and_11_out, and_12_out, and_13_out);

  // Notes on the sheet:
  //   a)
  //   b)
  //   c)
  //   d)
  //   e)
endmodule

module Q2 (
  input  x,
  input  x_2,
  input  y,
  input  y_2,
  input  z,
  input  z_2,
  input  x_3,
  input  y_3,
  input  x_4,
  input  z_3,
  input  y_4,
  input  z_4,
  input  x_5,
  input  y_5,
  input  z_5,
  output out_16,
  output out_17,
  output out_18,
  output out_19,
  output out_20
);

  wire not_1_out, not_2_out, not_3_out, not_4_out, not_5_out, not_6_out, not_7_out, not_8_out, not_9_out,
       not_10_out, not_11_out, not_12_out, not_13_out, not_14_out, not_15_out, or_1_out, or_2_out, or_3_out,
       or_4_p3, or_5_out, or_6_out, or_7_out, or_8_out, or_9_out, or_10_out, or_11_out, or_12_out, or_13_out;

  not not_1 (not_1_out, x_5);
  not not_2 (not_2_out, y_5);
  not not_3 (not_3_out, z_5);
  not not_4 (not_4_out, x);
  not not_5 (not_5_out, y);
  not not_6 (not_6_out, z);
  not not_7 (not_7_out, x_3);
  not not_8 (not_8_out, y_3);
  not not_9 (not_9_out, z_3);
  or or_1 (or_1_out, x, not_6_out);
  or or_2 (or_2_out, not_5_out, not_6_out);
  or or_3 (or_3_out, not_7_out, y_3);
  // OR_Gate or_4: pin names not known; wires that end beside it: not_8_out, not_9_out, or_4_p3
  and and_1 (out_17, or_1_out, or_2_out);
  and and_2 (out_18, or_3_out, or_4_p3);
  or or_5 (or_5_out, x_5, not_2_out);
  or or_6 (or_6_out, not_1_out, z_5);
  or or_7 (or_7_out, not_2_out, z_5);
  and and_3 (out_20, or_6_out, or_7_out);
  not not_10 (not_10_out, x_2);
  not not_11 (not_11_out, y_2);
  not not_12 (not_12_out, z_2);
  not not_13 (not_13_out, x_4);
  not not_14 (not_14_out, y_4);
  not not_15 (not_15_out, z_4);
  or or_8 (or_8_out, not_10_out, not_11_out);
  or or_9 (or_9_out, not_10_out, z_2);
  or or_10 (or_10_out, not_11_out, not_12_out);
  or or_11 (or_11_out, not_13_out, y_4);
  or or_12 (or_12_out, not_13_out, not_15_out);
  or or_13 (or_13_out, y_4, not_15_out);
  and and_4 (out_16, or_8_out, or_9_out, or_10_out);
  and and_5 (out_19, or_11_out, or_12_out, or_13_out);

  // Notes on the sheet:
  //   a)
  //   b)
  //   c)
  //   nao consegui fazer 
  //   d)
  //   e)
endmodule

module Q3 (
  input  x,
  input  y,
  input  z,
  input  w,
  output a,
  output b,
  output c,
  output d,
  output e
);

  wire and_1_out, and_2_out, and_3_out, and_4_out, and_5_out, and_6_out, and_7_out, and_8_out, and_9_out,
       and_10_out, and_11_out, and_12_out, and_13_out, and_14_out, and_15_out, and_16_out, and_17_out,
       and_18_out, and_19_out, and_20_out, and_21_out, and_22_out, and_23_out, and_24_out, and_25_out,
       and_26_out, and_27_out, and_28_out, and_29_out, and_30_out, not_1_out, not_2_out, not_3_out,
       not_4_out, not_5_out, not_6_out, not_7_out, not_8_out, not_9_out, not_10_out, not_11_out, not_12_out,
       not_13_out, not_14_out, not_15_out, not_16_out, not_17_out, not_18_out, not_19_out, not_20_out,
       not_21_out, not_22_out, not_23_out, not_24_out, not_25_out, not_26_out, not_27_out, not_28_out,
       not_29_out, not_30_out, not_31_out, not_32_out, not_33_out, not_34_out, not_35_out, not_36_out,
       not_37_out, not_38_out, not_39_out, not_40_out, not_41_out, not_42_out, not_43_out, not_44_out,
       not_45_out, not_46_out;

  not not_1 (not_1_out, x);
  not not_2 (not_2_out, z);
  not not_3 (not_3_out, y);
  not not_4 (not_4_out, z);
  not not_5 (not_5_out, x);
  not not_6 (not_6_out, z);
  not not_7 (not_7_out, z);
  not not_8 (not_8_out, x);
  not not_9 (not_9_out, y);
  not not_10 (not_10_out, z);
  not not_11 (not_11_out, y);
  not not_12 (not_12_out, z);
  not not_13 (not_13_out, z);
  not not_14 (not_14_out, x);
  not not_15 (not_15_out, z);
  not not_16 (not_16_out, z);
  not not_17 (not_17_out, z);
  not not_18 (not_18_out, x);
  not not_19 (not_19_out, y);
  not not_20 (not_20_out, w);
  not not_21 (not_21_out, z);
  not not_22 (not_22_out, y);
  not not_23 (not_23_out, z);
  not not_24 (not_24_out, z);
  not not_25 (not_25_out, x);
  not not_26 (not_26_out, z);
  not not_27 (not_27_out, x);
  not not_28 (not_28_out, w);
  not not_29 (not_29_out, x);
  not not_30 (not_30_out, z);
  not not_31 (not_31_out, y);
  not not_32 (not_32_out, z);
  not not_33 (not_33_out, x);
  not not_34 (not_34_out, z);
  not not_35 (not_35_out, x);
  not not_36 (not_36_out, y);
  not not_37 (not_37_out, w);
  not not_38 (not_38_out, z);
  not not_39 (not_39_out, y);
  not not_40 (not_40_out, w);
  not not_41 (not_41_out, z);
  not not_42 (not_42_out, x);
  not not_43 (not_43_out, w);
  not not_44 (not_44_out, w);
  not not_45 (not_45_out, z);
  not not_46 (not_46_out, z);
  and and_1 (and_1_out, not_1_out, w, not_2_out);
  and and_2 (and_2_out, x, not_3_out, w, not_4_out);
  and and_3 (and_3_out, not_5_out, y, not_6_out);
  and and_4 (and_4_out, x, w, z);
  and and_5 (and_5_out, x, y, w, not_7_out);
  and and_6 (and_6_out, not_8_out, not_9_out, not_10_out);
  and and_7 (and_7_out, x, not_11_out, not_12_out);
  and and_8 (and_8_out, x, y, not_13_out);
  and and_9 (and_9_out, not_14_out, w, not_15_out);
  and and_10 (and_10_out, x, w, not_16_out);
  and and_11 (and_11_out, x, y, w, not_17_out);
  and and_12 (and_12_out, not_18_out, not_19_out, not_20_out, not_21_out);
  and and_13 (and_13_out, x, not_22_out, w, not_23_out);
  and and_14 (and_14_out, x, y, not_24_out);
  and and_15 (and_15_out, not_25_out, w, z);
  and and_16 (and_16_out, x, w, not_26_out);
  and and_17 (and_17_out, not_27_out, not_28_out, z);
  and and_18 (and_18_out, not_29_out, y, w, not_30_out);
  and and_19 (and_19_out, x, not_31_out, w, z);
  and and_20 (and_20_out, x, y, not_32_out);
  and and_21 (and_21_out, not_33_out, w, z);
  and and_22 (and_22_out, x, w, not_34_out);
  and and_23 (and_23_out, x, w, z);
  and and_24 (and_24_out, not_35_out, not_36_out, not_37_out, not_38_out);
  and and_25 (and_25_out, x, not_39_out, not_40_out, z);
  and and_26 (and_26_out, x, y, not_41_out);
  and and_27 (and_27_out, not_42_out, not_43_out, z);
  and and_28 (and_28_out, x, not_44_out, not_45_out);
  and and_29 (and_29_out, x, w, not_46_out);
  and and_30 (and_30_out, x, w, z);
  or or_1 (a, and_1_out, and_2_out, and_3_out, and_4_out, and_5_out);
  or or_2 (b, and_6_out, and_7_out, and_8_out, and_9_out, and_10_out, and_11_out);
  or or_3 (c, and_12_out, and_13_out, and_14_out, and_15_out, and_16_out, and_17_out);
  or or_4 (d, and_18_out, and_19_out, and_20_out, and_21_out, and_22_out, and_23_out);
  or or_5 (e, and_24_out, and_25_out, and_26_out, and_27_out, and_28_out, and_29_out, and_30_out);
endmodule

module Q4 (
  input  X,
  input  Y,
  input  Z,
  input  W,
  output a,
  output b,
  output c,
  output d,
  output e
);

  wire and_1_out, and_2_out, and_3_out, and_4_out, and_5_out, and_6_out, and_7_out, and_8_out, and_9_out,
       and_10_out, and_11_out, and_12_out, and_13_out, and_14_out, and_15_out, and_16_out, and_17_out,
       and_18_out, and_19_out, and_20_out, and_21_out, and_22_out, and_23_out, and_24_out, and_25_out,
       and_26_out, not_1_out, not_2_out, not_3_out, not_4_out, not_5_out, not_6_out, not_7_out, not_8_out,
       not_9_out, not_10_out, not_11_out, not_12_out, not_13_out, not_14_out, not_15_out, not_16_out,
       not_17_out, not_18_out, not_19_out, not_20_out, not_21_out, not_22_out, not_23_out, not_24_out,
       not_25_out, not_26_out, not_27_out, not_28_out, not_29_out, not_30_out, not_31_out, not_32_out,
       not_33_out, not_34_out, not_35_out, not_36_out, not_37_out, not_38_out, not_39_out, not_40_out,
       not_41_out, not_42_out, not_43_out, not_44_out, not_45_out, not_46_out, not_47_out, not_48_out,
       not_49_out, not_50_out, not_51_out, not_52_out, not_53_out, not_54_out, not_55_out, not_56_out,
       not_57_out, not_58_out, not_59_out, not_60_out, not_61_out, not_62_out, not_63_out, not_64_out,
       not_65_out, not_66_out, not_67_out, not_68_out, not_69_out, not_70_out;

  not not_1 (not_1_out, X);
  not not_2 (not_2_out, Y);
  not not_3 (not_3_out, Y);
  not not_4 (not_4_out, W);
  not not_5 (not_5_out, Z);
  not not_6 (not_6_out, W);
  not not_7 (not_7_out, Z);
  not not_8 (not_8_out, X);
  not not_9 (not_9_out, X);
  not not_10 (not_10_out, Z);
  not not_11 (not_11_out, X);
  not not_12 (not_12_out, Y);
  not not_13 (not_13_out, X);
  not not_14 (not_14_out, X);
  not not_15 (not_15_out, Y);
  not not_16 (not_16_out, W);
  not not_17 (not_17_out, X);
  not not_18 (not_18_out, Y);
  not not_19 (not_19_out, W);
  not not_20 (not_20_out, Z);
  not not_21 (not_21_out, X);
  not not_22 (not_22_out, Z);
  not not_23 (not_23_out, X);
  not not_24 (not_24_out, Y);
  not not_25 (not_25_out, Z);
  not not_26 (not_26_out, X);
  not not_27 (not_27_out, Y);
  not not_28 (not_28_out, W);
  not not_29 (not_29_out, Z);
  not not_30 (not_30_out, X);
  not not_31 (not_31_out, Y);
  not not_32 (not_32_out, W);
  not not_33 (not_33_out, X);
  not not_34 (not_34_out, Y);
  not not_35 (not_35_out, W);
  not not_36 (not_36_out, Z);
  not not_37 (not_37_out, Y);
  not not_38 (not_38_out, Y);
  not not_39 (not_39_out, W);
  not not_40 (not_40_out, Z);
  not not_41 (not_41_out, Y);
  not not_42 (not_42_out, W);
  not not_43 (not_43_out, X);
  not not_44 (not_44_out, Y);
  not not_45 (not_45_out, W);
  not not_46 (not_46_out, Z);
  not not_47 (not_47_out, X);
  not not_48 (not_48_out, Y);
  not not_49 (not_49_out, W);
  not not_50 (not_50_out, Z);
  not not_51 (not_51_out, X);
  not not_52 (not_52_out, Y);
  not not_53 (not_53_out, W);
  not not_54 (not_54_out, X);
  not not_55 (not_55_out, Y);
  not not_56 (not_56_out, Y);
  not not_57 (not_57_out, W);
  not not_58 (not_58_out, Z);
  not not_59 (not_59_out, Y);
  not not_60 (not_60_out, W);
  not not_61 (not_61_out, Z);
  not not_62 (not_62_out, Y);
  not not_63 (not_63_out, W);
  not not_64 (not_64_out, X);
  not not_65 (not_65_out, Y);
  not not_66 (not_66_out, W);
  not not_67 (not_67_out, Z);
  not not_68 (not_68_out, X);
  not not_69 (not_69_out, Y);
  not not_70 (not_70_out, Z);
  and and_1 (and_1_out, not_1_out, not_2_out, Z);
  and and_2 (and_2_out, X, not_3_out, not_4_out, not_5_out);
  and and_3 (and_3_out, X, Y, not_6_out, not_7_out);
  and and_4 (and_4_out, not_8_out, Y, W, Z);
  and and_5 (and_5_out, not_9_out, Y, not_10_out);
  and and_6 (and_6_out, not_11_out, not_12_out, Z, W);
  and and_7 (and_7_out, not_13_out, Y, W, Z);
  and and_8 (and_8_out, not_14_out, not_15_out, not_16_out, Z);
  and and_9 (and_9_out, not_17_out, not_18_out, not_19_out, not_20_out);
  and and_10 (and_10_out, not_21_out, Y, not_22_out);
  and and_11 (and_11_out, not_23_out, not_24_out, W, not_25_out);
  and and_12 (and_12_out, not_26_out, not_27_out, not_28_out, not_29_out);
  and and_13 (and_13_out, not_30_out, not_31_out, not_32_out, Z);
  and and_14 (and_14_out, not_33_out, not_34_out, not_35_out, not_36_out);
  and and_15 (and_15_out, X, not_37_out, Z);
  and and_16 (and_16_out, X, not_38_out, not_39_out, not_40_out);
  and and_17 (and_17_out, X, not_41_out, not_42_out, Z);
  and and_18 (and_18_out, not_43_out, not_44_out, not_45_out, not_46_out);
  and and_19 (and_19_out, not_47_out, not_48_out, not_49_out, not_50_out);
  and and_20 (and_20_out, not_51_out, not_52_out, not_53_out, Z);
  and and_21 (and_21_out, not_54_out, not_55_out, W, Z);
  and and_22 (and_22_out, X, not_56_out, not_57_out, not_58_out);
  and and_23 (and_23_out, X, not_59_out, not_60_out, not_61_out);
  and and_24 (and_24_out, X, not_62_out, not_63_out, Z);
  and and_25 (and_25_out, not_64_out, not_65_out, not_66_out, not_67_out);
  and and_26 (and_26_out, not_68_out, not_69_out, W, not_70_out);
  or or_1 (a, and_1_out, and_2_out, and_3_out, and_4_out);
  or or_2 (b, and_5_out, and_6_out, and_7_out, and_8_out, and_9_out);
  or or_3 (c, and_10_out, and_11_out, and_12_out, and_13_out, and_14_out);
  or or_4 (d, and_15_out, and_16_out, and_17_out, and_18_out, and_19_out, and_20_out);
  or or_5 (e, and_21_out, and_22_out, and_23_out, and_24_out, and_25_out, and_26_out);
endmodule

module Q5 (
  input  x,
  input  y,
  input  z,
  output s
);

  wire not_1_out, not_2_out, not_3_out, not_4_out;

  not not_1 (not_1_out, x);
  not not_2 (not_2_out, z);
  not not_3 (not_3_out, x);
  not not_4 (not_4_out, y);
  and and_1 (s, not_1_out, not_2_out, not_3_out, not_4_out);
endmodule

module Q6 (
  input  X,
  input  Y,
  input  W,
  input  Z,
  output s
);

  wire and_1_out, and_2_out, and_3_out, not_1_out, not_2_out, not_3_out;

  and and_1 (and_1_out, X, not_1_out);
  not not_1 (not_1_out, Y);
  and and_2 (and_2_out, X, not_2_out);
  not not_2 (not_2_out, W);
  and and_3 (and_3_out, X, not_3_out);
  not not_3 (not_3_out, Z);
  or or_1 (s, and_1_out, and_2_out, and_3_out);
endmodule
