// Logisim project Logisim.circ as structural Verilog: 5 circuits, main circuit Guia_0701
module Guia_0701 (
  input  in_1,
  input  in_2,
  input  Chave,
  output out_4
);

  wire and_1_out, and_2_out, and_3_out, and_4_out, not_1_out, not_2_out;

  and and_1 (and_1_out, in_1, in_2);
  and and_2 (and_2_out, in_1, in_2);
  not not_1 (not_1_out, and_2_out);
  not not_2 (not_2_out, Chave);
  and and_3 (and_3_out, and_1_out, not_2_out);
  and and_4 (and_4_out, Chave, not_1_out);
  or or_1 (out_4, and_3_out, and_4_out);

  // Notes on the sheet:
  //   AND
  //   NAND
  //   Mux
endmodule

module Guia_0702 (
  input  in_1,
  input  in_2,
  input  Chave,
  output out_4
);

  wire and_1_out, and_2_out, not_1_out, not_2_out, or_1_out, or_2_out;

  or or_1 (or_1_out, in_1, in_2);
  or or_2 (or_2_out, in_1, in_2);
  not not_1 (not_1_out, or_2_out);
  not not_2 (not_2_out, Chave);
  and and_1 (and_1_out, or_1_out, not_2_out);
  and and_2 (and_2_out, Chave, not_1_out);
  or or_3 (out_4, and_1_out, and_2_out);

  // Notes on the sheet:
  //   OR
  //   NOR
  //   Mux
endmodule

module Guia_0703 (
  input  Chave,
  input  in_2,
  input  in_3,
  input  in_4,
  input  Chave_2,
  input  in_6,
  output out_7
);

  wire and_1_out, and_2_out, and_3_out, and_4_out, and_5_out, and_6_out, and_7_out, and_8_out, not_1_out,
       not_2_out, not_3_out, not_4_out, not_5_out, or_1_out, or_2_out, or_3_out, or_4_out;

  and and_1 (and_1_out, in_2, in_3);
  and and_2 (and_2_out, in_2, in_3);
  not not_1 (not_1_out, and_2_out);
  or or_1 (or_1_out, in_4, in_6);
  not not_2 (not_2_out, or_2_out);
  or or_2 (or_2_out, in_4, in_6);
  not not_3 (not_3_out, Chave);
  not not_4 (not_4_out, Chave);
  and and_3 (and_3_out, and_1_out, not_3_out);
  and and_4 (and_4_out, Chave, not_1_out);
  and and_5 (and_5_out, or_1_out, not_4_out);
  and and_6 (and_6_out, Chave, not_2_out);
  or or_3 (or_3_out, and_3_out, and_4_out);
  or or_4 (or_4_out, and_5_out, and_6_out);
  not not_5 (not_5_out, Chave_2);
  and and_7 (and_7_out, or_3_out, not_5_out);
  and and_8 (and_8_out, Chave_2, or_4_out);
  or or_5 (out_7, and_7_out, and_8_out);

  // Notes on the sheet:
  //   AND
  //   NAND
  //   OR
  //   NOR
  //   Mux
  //   Mux
  //   Mux
endmodule

module Guia_0704 (
  input  Chave,
  input  in_2,
  input  in_3,
  input  Chave_2,
  input  in_5,
  input  in_6,
  output out_7
);

  wire and_1_out, and_2_out, and_3_out, and_4_out, and_5_out, and_6_out, and_7_out, and_8_out, and_9_out,
       and_10_out, not_1_out, not_2_out, not_3_out, not_4_out, not_5_out, not_6_out, not_7_out, or_1_out,
       or_2_out, or_3_out, or_4_out, or_5_out, or_6_out;

  or or_1 (or_1_out, in_2, in_3);
  not not_1 (not_1_out, and_1_out);
  and and_1 (and_1_out, in_2, in_3);
  or or_2 (or_2_out, in_2, in_3);
  not not_2 (not_2_out, and_2_out);
  and and_2 (and_2_out, in_2, in_2);
  or or_3 (or_3_out, in_5, in_6);
  not not_3 (not_3_out, or_4_out);
  or or_4 (or_4_out, in_5, in_6);
  and and_3 (and_3_out, or_1_out, not_1_out);
  not not_4 (not_4_out, and_4_out);
  and and_4 (and_4_out, or_2_out, not_2_out);
  not not_5 (not_5_out, Chave);
  not not_6 (not_6_out, Chave);
  and and_5 (and_5_out, and_3_out, not_5_out);
  and and_6 (and_6_out, Chave, not_4_out);
  and and_7 (and_7_out, or_3_out, not_6_out);
  and and_8 (and_8_out, Chave, not_3_out);
  or or_5 (or_5_out, and_5_out, and_6_out);
  or or_6 (or_6_out, and_7_out, and_8_out);
  not not_7 (not_7_out, Chave_2);
  and and_9 (and_9_out, or_5_out, not_7_out);
  and and_10 (and_10_out, Chave_2, or_6_out);
  or or_7 (out_7, and_9_out, and_10_out);

  // Notes on the sheet:
  //   XOR
  //   XNOR
  //   OR
  //   NOR
  //   Mux
  //   Mux
  //   Mux
endmodule

module Guia_0705 (
  input  a,
  input  b,
  input  [2:0] in_3,
  output sFinal
);

  wire and_1_out, and_2_out, and_3_out, nand_1_out, nand_2_out, nand_3_out, nor_1_out, nor_2_out, or_1_out,
       or_2_out;

  and and_1 (and_1_out, a, b);
  nand nand_1 (nand_1_out, a, b);
  or or_1 (or_1_out, a, b);
  nand nand_2 (nand_2_out, a, b);
  nor nor_1 (nor_1_out, a, b);
  nand nand_3 (nand_3_out, a, b);
  or or_2 (or_2_out, a, b);
  nor nor_2 (nor_2_out, a, b);
  and and_2 (and_2_out, or_1_out, nand_2_out);
  and and_3 (and_3_out, nor_1_out, nand_3_out);
  Multiplexer #(.select(3)) multiplexer_1 (
    .in0(1'b0), .in1(and_1_out), .in2(nand_1_out), .in3(and_2_out), .in4(and_3_out), .in5(or_2_out),
    .in6(nor_2_out), .in7(1'b0), .out(sFinal), .sel(in_3));  // open: en
endmodule
