// Logisim project Logisim.circ as structural Verilog: 4 circuits, main circuit main
module main (
  input  A,
  input  B,
  input  VEM,
  output S,
  output VAI
);

  wire and_1_out, and_2_out, and_3_out, and_4_out, and_5_out, and_6_out, and_7_out, and_8_out, not_1_out,
       not_2_out, not_3_out, or_1_out, or_3_out, or_4_out, or_6_out;

  not not_1 (not_1_out, A);
  not not_2 (not_2_out, B);
  not not_3 (not_3_out, VEM);
  and and_1 (and_1_out, not_1_out, not_2_out, VEM);
  and and_2 (and_2_out, not_1_out, B, not_3_out);
  and and_3 (and_3_out, A, not_2_out, not_3_out);
  and and_4 (and_4_out, A, B, VEM);
  and and_5 (and_5_out, not_1_out, B, VEM);
  and and_6 (and_6_out, A, not_2_out, VEM);
  and and_7 (and_7_out, A, B, B, not_3_out);
  and and_8 (and_8_out, A, A, B, VEM);
  or or_1 (or_1_out, and_1_out, and_2_out);
  or or_2 (S, or_1_out, or_3_out);
  or or_3 (or_3_out, and_3_out, and_4_out);
  or or_4 (or_4_out, and_5_out, and_6_out);
  or or_5 (VAI, or_4_out, or_6_out);
  or or_6 (or_6_out, and_7_out, and_8_out);

  // Notes on the sheet:
  //   Somador de 1 bit
endmodule

module Guia_0801 (
  input  in_1,
  input  in_2,
  input  in_3,
  input  in_4,
  input  in_5,
  input  in_6,
  input  in_7,
  input  in_8,
  input  B,
  input  in_10,
  input  in_11,
  input  in_12,
  output out_13,
  output out_14,
  output out_15,
  output out_16,
  output out_17,
  output out_18
);

  wire main_2_vai, main_3_vai, main_4_vai, main_5_vai, main_6_vai;

  main main_1 (.S(out_13), .A(in_1), .B(in_7), .VEM(main_2_vai));  // open: VAI
  main main_2 (.S(out_14), .VAI(main_2_vai), .A(in_2), .B(in_8), .VEM(main_3_vai));
  main main_3 (.S(out_15), .VAI(main_3_vai), .A(in_3), .B(B), .VEM(main_4_vai));
  main main_4 (.S(out_16), .VAI(main_4_vai), .A(in_4), .B(in_10), .VEM(main_5_vai));
  main main_5 (.S(out_17), .VAI(main_5_vai), .A(in_5), .B(in_11), .VEM(main_6_vai));
  main main_6 (.S(out_18), .VAI(main_6_vai), .A(in_6), .B(in_12), .VEM(1'b0));

  // Notes on the sheet:
  //   Somador completo
  //   A
endmodule

module Guia_0802 (
  input  Num1,
  input  in_2,
  input  in_3,
  input  in_4,
  input  in_5,
  input  Num2,
  input  in_7,
  input  in_8,
  input  in_9,
  input  in_10,
  input  in_11,
  input  in_12,
  output x,
  output y,
  output z,
  output u,
  output v,
  output w
);

  wire and_1_out, and_2_out, and_3_out, and_4_out, and_5_out, and_6_out, and_7_out, and_8_out, and_9_out,
       and_10_out, and_11_out, and_12_out, and_13_out, and_14_out, and_15_out, and_16_out, and_17_out,
       and_18_out, and_19_out, and_20_out, and_21_out, and_22_out, and_23_out, and_24_out, and_25_out,
       and_26_out, and_27_out, and_28_out, and_29_out, and_30_out, and_31_out, and_32_out, and_33_out,
       and_34_out, and_35_out, and_36_out, and_37_out, and_38_out, and_39_out, and_40_out, and_41_out,
       and_42_out, and_43_out, and_44_out, and_45_out, and_46_out, and_47_out, not_1_out, not_2_out,
       not_3_out, not_4_out, not_5_out, not_6_out, not_7_out, not_8_out, not_9_out, not_10_out, not_11_out,
       not_12_out, not_13_out, not_14_out, not_15_out, not_16_out, not_17_out, not_18_out, not_19_out,
       not_20_out, not_21_out, not_22_out, not_23_out, not_24_out, not_25_out, not_26_out, not_27_out,
       not_28_out, not_29_out, not_30_out, not_31_out, not_32_out, not_33_out, not_34_out, not_35_out,
       not_36_out, not_37_out, not_38_out, not_39_out, not_40_out;

  and and_1 (and_1_out, Num1, in_2, in_4, in_5, in_7, in_9, in_11);
  and and_2 (and_2_out, Num1, in_2, in_4, in_5, Num2, in_7, in_9, in_12);
  and and_3 (and_3_out, Num1, in_2, in_3, in_7, in_9);
  and and_4 (and_4_out, Num1, in_2, in_3, Num2, in_7, in_10, in_11, in_12);
  and and_5 (and_5_out, Num1, in_2, in_3, in_5, in_7, in_10, in_11);
  and and_6 (and_6_out, Num1, in_2, in_3, in_5, Num2, in_7, in_10, in_12);
  and and_7 (and_7_out, Num1, in_2, in_3, in_4, in_7, in_10);
  and and_8 (and_8_out, Num1, in_2, in_3, in_4, Num2, in_7, in_11, in_12);
  and and_9 (and_9_out, Num1, in_2, in_3, in_4, in_5, in_7, in_11);
  and and_10 (and_10_out, Num1, in_2, in_3, in_4, in_5, Num2, in_7);
  and and_11 (and_11_out, in_2, in_4, in_5, Num2, in_8, in_9, in_12);
  and and_12 (and_12_out, in_2, in_3, in_8, in_9);
  and and_13 (and_13_out, in_2, in_3, Num2, in_8, in_10, in_11, in_12);
  and and_14 (and_14_out, in_2, in_3, in_5, in_8, in_10, in_11);
  and and_15 (and_15_out, in_2, in_3, in_5, Num2, in_8, in_10, in_12);
  and and_16 (and_16_out, in_2, in_3, in_4, in_8, in_10);
  and and_17 (and_17_out, in_2, in_3, in_4, Num2, in_8, in_11, in_12);
  and and_18 (and_18_out, in_2, in_3, in_4, in_5, in_8, in_11);
  and and_19 (and_19_out, in_2, in_3, in_4, in_5, Num2, in_8, in_12);
  not not_1 (not_1_out, in_10);
  not not_2 (not_2_out, in_12);
  not not_3 (not_3_out, Num2);
  not not_4 (not_4_out, in_9);
  not not_5 (not_5_out, in_10);
  not not_6 (not_6_out, in_11);
  not not_7 (not_7_out, in_9);
  not not_8 (not_8_out, in_10);
  not not_9 (not_9_out, in_11);
  not not_10 (not_10_out, in_12);
  not not_11 (not_11_out, in_10);
  not not_12 (not_12_out, in_4);
  not not_13 (not_13_out, in_10);
  not not_14 (not_14_out, in_5);
  not not_15 (not_15_out, Num2);
  not not_16 (not_16_out, in_10);
  not not_17 (not_17_out, in_5);
  not not_18 (not_18_out, in_10);
  not not_19 (not_19_out, in_11);
  not not_20 (not_20_out, in_5);
  not not_21 (not_21_out, in_10);
  not not_22 (not_22_out, in_12);
  not not_23 (not_23_out, Num2);
  not not_24 (not_24_out, in_10);
  not not_25 (not_25_out, in_11);
  not not_26 (not_26_out, in_10);
  not not_27 (not_27_out, in_11);
  not not_28 (not_28_out, in_12);
  not not_29 (not_29_out, in_5);
  not not_30 (not_30_out, Num2);
  not not_31 (not_31_out, in_5);
  not not_32 (not_32_out, in_12);
  not not_33 (not_33_out, in_5);
  not not_34 (not_34_out, in_11);
  not not_35 (not_35_out, Num2);
  not not_36 (not_36_out, in_11);
  not not_37 (not_37_out, in_11);
  not not_38 (not_38_out, in_12);
  not not_39 (not_39_out, Num2);
  and and_20 (and_20_out, not_39_out, in_12);
  and and_21 (and_21_out, Num2, not_40_out);
  not not_40 (not_40_out, in_12);
  or or_1 (x, and_1_out, and_2_out, and_3_out, and_4_out, and_5_out, and_6_out, and_7_out, and_8_out, and_9_out, and_10_out);
  or or_2 (y, and_11_out, and_12_out, and_13_out, and_14_out, and_15_out, and_16_out, and_17_out, and_18_out, and_19_out);
  and and_22 (and_22_out, not_1_out, not_2_out);
  and and_23 (and_23_out, in_3, not_3_out, not_4_out, not_5_out, not_6_out);
  and and_24 (and_24_out, in_3, not_7_out, not_8_out, not_9_out, not_10_out);
  and and_25 (and_25_out, in_3, Num2, in_9, in_10, in_11, in_12);
  and and_26 (and_26_out, in_3, in_5, in_9, in_10, in_11);
  and and_27 (and_27_out, in_3, in_5, Num2, in_9, in_10, in_12);
  and and_28 (and_28_out, in_3, in_4, in_9, in_10);
  and and_29 (and_29_out, in_3, in_4, Num2, in_9, in_11, in_12);
  and and_30 (and_30_out, in_3, in_4, in_5, in_9, in_11);
  and and_31 (and_31_out, in_3, in_4, in_5, Num2, in_9, in_12);
  and and_32 (and_32_out, in_5, not_11_out, in_11);
  and and_33 (and_33_out, not_12_out, in_5, Num2, not_13_out, in_12);
  and and_34 (and_34_out, in_4, not_14_out, not_15_out, not_16_out);
  and and_35 (and_35_out, in_4, not_17_out, not_18_out, not_19_out);
  and and_36 (and_36_out, in_4, not_20_out, not_21_out, not_22_out);
  and and_37 (and_37_out, in_4, not_23_out, not_24_out, not_25_out);
  and and_38 (and_38_out, in_4, not_26_out, not_27_out, not_28_out);
  and and_39 (and_39_out, in_4, Num2, in_10, in_11, in_12);
  and and_40 (and_40_out, in_4, in_5, in_10, in_11);
  and and_41 (and_41_out, in_4, in_5, Num2, in_10, in_12);
  and and_42 (and_42_out, not_29_out, not_30_out, in_11);
  and and_43 (and_43_out, not_31_out, in_11, not_32_out);
  and and_44 (and_44_out, not_33_out, Num2, not_34_out, in_12);
  and and_45 (and_45_out, in_5, not_35_out, not_36_out);
  and and_46 (and_46_out, in_5, not_37_out, not_38_out);
  and and_47 (and_47_out, in_5, Num2, in_11, in_12);
  or or_3 (w, and_20_out, and_21_out);
  or or_4 (z, and_22_out, and_23_out, and_24_out, and_25_out, and_26_out, and_27_out, and_28_out, and_29_out, and_30_out, and_31_out);
  or or_5 (u, and_32_out, and_33_out, and_34_out, and_35_out, and_36_out, and_37_out, and_38_out, and_39_out, and_40_out, and_41_out);
  or or_6 (v, and_42_out, and_43_out, and_44_out, and_45_out, and_46_out, and_47_out);
endmodule

module subtrador (
  input  in_1,
  input  in_2,
  input  in_3,
  output out_4,
  output out_5
);

  wire and_1_out, and_2_out, and_3_out, not_1_out, not_2_out, xor_1_out;

  not not_1 (not_1_out, in_1);
  and and_1 (and_1_out, not_1_out, in_3);
  not not_2 (not_2_out, in_1);
  and and_2 (and_2_out, not_2_out, in_2, in_2);
  and and_3 (and_3_out, in_2, in_3);
  xor xor_1 (xor_1_out, in_1, in_2);
  xor xor_2 (out_4, xor_1_out, in_3);
  or or_1 (out_5, and_1_out, and_2_out, and_3_out);
endmodule
