// Logisim project q05b.circ as structural Verilog: 1 circuit, main circuit main
module main (
  input  in_1,
  input  in_2,
  input  in_3,
  output out_4
);

  wire nor_1_out, not_1_out, not_2_out;

  not not_1 (not_1_out, in_1);
  not not_2 (not_2_out, in_2);
  nor nor_1 (nor_1_out, not_1_out, not_2_out);
  nor nor_2 (out_4, nor_1_out, in_3);
endmodule
