// Logisim project somadores.circ as structural Verilog
module meia_soma (
  input  x0,
  input  y0,
  output s0,
  output Carry_Out
);

  xor xor_1 (s0, x0, y0);
  and and_1 (Carry_Out, y0, x0);
endmodule

module soma_completa (
  input  Vem1,
  input  x1,
  input  y1,
  output out_4,
  output out_5
);

  wire meia_soma_1_carry_out, meia_soma_1_s0, meia_soma_2_carry_out;

  meia_soma meia_soma_1 (.x0(x1), .y0(y1), .s0(meia_soma_1_s0), .Carry_Out(meia_soma_1_carry_out));
  meia_soma meia_soma_2 (.x0(Vem1), .y0(meia_soma_1_s0), .s0(out_4), .Carry_Out(meia_soma_2_carry_out));
  or or_1 (out_5, meia_soma_1_carry_out, meia_soma_2_carry_out);
endmodule

module soma_4bits (
  input  ci,
  input  x0,
  input  y0,
  input  x1,
  input  y1,
  input  x2,
  input  y2,
  input  x3,
  input  y3,
  output out_10,
  output out_11,
  output out_12,
  output out_13,
  output out_14
);

  wire soma_completa_1_out_5, soma_completa_2_out_5, soma_completa_3_out_5;

  soma_completa soma_completa_1 (.x1(x0), .y1(y0), .Vem1(ci), .out_5(soma_completa_1_out_5), .out_4(out_10));
  soma_completa soma_completa_2 (
    .x1(x1), .y1(y1), .Vem1(soma_completa_1_out_5), .out_5(soma_completa_2_out_5), .out_4(out_11));
  soma_completa soma_completa_3 (
    .x1(x2), .y1(y2), .Vem1(soma_completa_2_out_5), .out_5(soma_completa_3_out_5), .out_4(out_12));
  soma_completa soma_completa_4 (.x1(x3), .y1(y3), .Vem1(soma_completa_3_out_5), .out_5(out_14), .out_4(out_13));
endmodule

module decodificador_hexa (
  input  A0,
  input  A1,
  input  A2,
  input  A3,
  output a,
  output b,
  output c,
  output d,
  output e,
  output f,
  output g
);

  wire and_1_out, and_2_out, and_3_out, and_4_out, and_5_out, and_6_out, and_7_out, and_8_out, and_9_out,
       and_10_out, and_11_out, and_12_out, and_13_out, and_14_out, and_15_out, and_16_out, and_17_out,
       and_18_out, and_19_out, and_20_out, and_21_out, and_22_out, and_23_out, and_24_out, and_25_out,
       and_26_out, and_27_out, and_28_out, and_29_out, and_30_out, and_31_out, and_32_out, and_33_out,
       and_34_out, and_35_out, and_36_out, not_1_out, not_2_out, not_3_out, not_4_out, not_5_out, not_6_out,
       not_7_out, not_8_out, not_9_out, not_10_out, not_11_out, not_12_out, not_13_out, not_14_out,
       not_15_out, not_16_out, not_17_out, not_18_out, not_19_out, not_20_out, not_21_out, not_22_out,
       not_23_out, not_24_out, not_25_out, not_26_out, not_27_out, not_28_out, not_29_out, not_30_out,
       not_31_out, not_32_out, not_33_out, not_34_out, not_35_out, not_36_out, not_37_out, not_38_out,
       not_39_out, not_40_out, not_41_out, not_42_out, not_43_out, not_44_out, not_45_out, not_46_out;

  not not_1 (not_1_out, A1);
  and and_1 (and_1_out, not_1_out, not_2_out);
  not not_2 (not_2_out, A3);
  not not_3 (not_3_out, A0);
  and and_2 (and_2_out, not_3_out, A2);
  not not_4 (not_4_out, A0);
  and and_3 (and_3_out, not_4_out, A1, A3);
  and and_4 (and_4_out, A1, A2);
  not not_5 (not_5_out, A1);
  and and_5 (and_5_out, A0, not_5_out, not_6_out);
  not not_6 (not_6_out, A2);
  and and_6 (and_6_out, A0, not_7_out);
  not not_7 (not_7_out, A3);
  not not_8 (not_8_out, A0);
  and and_7 (and_7_out, not_8_out, not_9_out);
  not not_9 (not_9_out, A1);
  not not_10 (not_10_out, A0);
  not not_11 (not_11_out, A2);
  and and_8 (and_8_out, not_10_out, not_11_out, not_12_out);
  not not_12 (not_12_out, A3);
  not not_13 (not_13_out, A1);
  and and_9 (and_9_out, not_13_out, not_14_out);
  not not_14 (not_14_out, A2);
  not not_15 (not_15_out, A1);
  and and_10 (and_10_out, not_15_out, not_16_out);
  not not_16 (not_16_out, A3);
  not not_17 (not_17_out, A0);
  and and_11 (and_11_out, not_17_out, A2, A3);
  not not_18 (not_18_out, A2);
  and and_12 (and_12_out, A0, not_18_out, A3);
  not not_19 (not_19_out, A0);
  and and_13 (and_13_out, not_19_out, not_20_out);
  not not_20 (not_20_out, A2);
  not not_21 (not_21_out, A0);
  and and_14 (and_14_out, not_21_out, A3);
  not not_22 (not_22_out, A2);
  and and_15 (and_15_out, not_22_out, A3);
  not not_23 (not_23_out, A0);
  and and_16 (and_16_out, not_23_out, A1);
  and and_17 (and_17_out, A0, not_24_out);
  not not_24 (not_24_out, A1);
  not not_25 (not_25_out, A0);
  and and_18 (and_18_out, not_25_out, not_26_out, not_27_out);
  not not_26 (not_26_out, A1);
  not not_27 (not_27_out, A3);
  not not_28 (not_28_out, A1);
  and and_19 (and_19_out, not_28_out, A2, A3);
  and and_20 (and_20_out, A1, not_29_out, A3);
  not not_29 (not_29_out, A2);
  and and_21 (and_21_out, A1, A2, not_30_out);
  not not_30 (not_30_out, A3);
  not not_31 (not_31_out, A2);
  and and_22 (and_22_out, A0, not_31_out, not_32_out);
  not not_32 (not_32_out, A3);
  not not_33 (not_33_out, A1);
  and and_23 (and_23_out, not_33_out, not_34_out);
  not not_34 (not_34_out, A3);
  and and_24 (and_24_out, A2, not_35_out);
  not not_35 (not_35_out, A3);
  and and_25 (and_25_out, A0, A2);
  and and_26 (and_26_out, A0, A1);
  not not_36 (not_36_out, A2);
  and and_27 (and_27_out, not_36_out, not_37_out);
  not not_37 (not_37_out, A3);
  not not_38 (not_38_out, A0);
  and and_28 (and_28_out, not_38_out, A1, not_39_out);
  not not_39 (not_39_out, A2);
  and and_29 (and_29_out, A1, not_40_out);
  not not_40 (not_40_out, A3);
  and and_30 (and_30_out, A0, not_41_out);
  not not_41 (not_41_out, A1);
  and and_31 (and_31_out, A0, A2);
  not not_42 (not_42_out, A1);
  and and_32 (and_32_out, not_42_out, A2);
  and and_33 (and_33_out, A2, not_43_out);
  not not_43 (not_43_out, A3);
  not not_44 (not_44_out, A0);
  and and_34 (and_34_out, not_44_out, A1, not_45_out);
  not not_45 (not_45_out, A2);
  and and_35 (and_35_out, A0, not_46_out);
  not not_46 (not_46_out, A1);
  and and_36 (and_36_out, A0, A3);
  or or_1 (c, and_13_out, and_14_out, and_15_out, and_16_out, and_17_out);
  or or_2 (d, and_18_out, and_19_out, and_20_out, and_21_out, and_22_out);
  or or_3 (e, and_23_out, and_24_out, and_25_out, and_26_out);
  or or_4 (f, and_27_out, and_28_out, and_29_out, and_30_out, and_31_out);
  or or_5 (g, and_32_out, and_33_out, and_34_out, and_35_out, and_36_out);
  or or_6 (a, and_1_out, and_2_out, and_3_out, and_4_out, and_5_out, and_6_out);
  or or_7 (b, and_7_out, and_8_out, and_9_out, and_10_out, and_11_out, and_12_out);
endmodule

module calculadora_4bits (
  input  A0,
  input  Ci,
  input  A1,
  input  A2,
  input  A3,
  input  B0,
  input  B1,
  input  B2,
  input  B3,
  output s0,
  output s1,
  output s2,
  output s3,
  output out_14
);

  wire decodificador_hexa_1_a, decodificador_hexa_1_b, decodificador_hexa_1_c, decodificador_hexa_1_d,
       decodificador_hexa_1_e, decodificador_hexa_1_f, decodificador_hexa_1_g;

  soma_4bits soma_4bits_1 (
    .ci(Ci), .x0(A0), .y0(B0), .x1(A1), .y1(B1), .x2(A2), .y2(B2), .x3(A3), .y3(B3), .out_14(out_14),
    .out_10(s0), .out_11(s1), .out_12(s2), .out_13(s3));
  decodificador_hexa decodificador_hexa_1 (
    .A0(B2), .A1(B2), .A2(B1), .A3(B0), .a(decodificador_hexa_1_a), .b(decodificador_hexa_1_b),
    .c(decodificador_hexa_1_c), .d(decodificador_hexa_1_d), .e(decodificador_hexa_1_e),
    .f(decodificador_hexa_1_f), .g(decodificador_hexa_1_g));
  _7_Segment_Display u_7_segment_display_1 (
    .g(decodificador_hexa_1_d), .f(decodificador_hexa_1_c), .a(decodificador_hexa_1_b),
    .b(decodificador_hexa_1_a), .e(decodificador_hexa_1_e), .d(decodificador_hexa_1_f),
    .c(decodificador_hexa_1_g));  // open: dp
endmodule
